# Fritzing sketch adc-rpi (saved by Fritzing 1.0.5)
breadboards: 1

parts:
  A1 = Raspberry Pi 5
  ADC1 = MCP3008 [package=dil16]  # not connected
  U1 = POT [knob_status=50% power=0.5W package=3362u]

nets:
  N1: A1.3V3, U1.A
  N2: A1.GND, U1.E

custom parts:
  Raspberry Pi 5: The RPi5, a faster version of the awesome Raspberry Pi4B ARM Board with 40 pin gpio.
