# Fritzing sketch dac-rpi (saved by Fritzing 1.0.5)
breadboards: 1

parts:
  A1 = Raspberry Pi 5
  A2 = Pcm5102A module

nets:
  N1: A1.3V3, A2.Pin_13
  N2: A1.5V, A1.Fan-5V, A2.Pin_6
  N3: A1.GND, A2.Pin_1, A2.Pin_5, A2.Pin_12
  N4: A1.GPIO18, A2.Pin_2
  N5: A1.GPIO19, A2.Pin_4
  N6: A1.GPIO21, A2.Pin_3

custom parts:
  Raspberry Pi 5: The RPi5, a faster version of the awesome Raspberry Pi4B ARM Board with 40 pin gpio.
  Pcm5102A module: Interface I2S PCM5102A DAC Decoder GY-PCM5102 I2S Player Module for Raspberry Pi pHAT Format Board Digital PCM5102 Audio Board.
